// Logisim project ETFStudent.circ as structural Verilog: 19 circuits, main circuit REG32_LD
module ALU16_ADD_SUB_NOT_AND_OR_XOR (
  input  Cin,
  input  [15:0] A,
  input  [15:0] B,
  input  add,
  input  sub,
  input  \not ,
  input  \and ,
  input  \or ,
  input  \xor ,
  output [15:0] F,
  output Cout
);

  wire adder_1_cout, subtractor_1_bout;
  wire [15:0] adder_1_out, and_1_out, negator_1_out, or_1_out, subtractor_1_out, xor_1_out;

  Adder #(.width(16)) adder_1 (.a(A), .b(B), .out(adder_1_out), .cin(Cin), .cout(adder_1_cout));
  Subtractor #(.width(16)) subtractor_1 (.a(A), .b(B), .out(subtractor_1_out), .bin(Cin), .bout(subtractor_1_bout));
  Negator #(.width(16)) negator_1 (.in(A), .out(negator_1_out));
  assign and_1_out = A & B;  // AND_Gate and_1, 16 bits wide
  assign or_1_out = A | B;  // OR_Gate or_1, 16 bits wide
  assign xor_1_out = A ^ B;  // XOR_Gate xor_1, 16 bits wide
  assign F = add ? adder_1_out : 16'bz;  // Controlled_Buffer controlled_buffer_1
  assign Cout = add ? adder_1_cout : 1'bz;  // Controlled_Buffer controlled_buffer_2
  assign F = sub ? subtractor_1_out : 16'bz;  // Controlled_Buffer controlled_buffer_3
  assign Cout = sub ? subtractor_1_bout : 1'bz;  // Controlled_Buffer controlled_buffer_4
  assign F = \not  ? negator_1_out : 16'bz;  // Controlled_Buffer controlled_buffer_5
  assign F = \and  ? and_1_out : 16'bz;  // Controlled_Buffer controlled_buffer_6
  assign F = \or  ? or_1_out : 16'bz;  // Controlled_Buffer controlled_buffer_7
  assign F = \xor  ? xor_1_out : 16'bz;  // Controlled_Buffer controlled_buffer_8
endmodule

module KMADR (
  input  immed,
  input  memdir,
  input  regdir,
  input  memind,
  input  preincr,
  input  postdec,
  input  regindpom,
  output [5:0] Adr5__0
);

  assign Adr5__0 = immed ? 6'b000010 : 6'bz;  // Controlled_Buffer controlled_buffer_1
  assign Adr5__0 = memdir ? 6'b000011 : 6'bz;  // Controlled_Buffer controlled_buffer_2
  assign Adr5__0 = memind ? 6'b000101 : 6'bz;  // Controlled_Buffer controlled_buffer_3
  assign Adr5__0 = regdir ? 6'b000100 : 6'bz;  // Controlled_Buffer controlled_buffer_4
  assign Adr5__0 = preincr ? 6'b001011 : 6'bz;  // Controlled_Buffer controlled_buffer_5
  assign Adr5__0 = postdec ? 6'b001111 : 6'bz;  // Controlled_Buffer controlled_buffer_6
  assign Adr5__0 = regindpom ? 6'b010011 : 6'bz;  // Controlled_Buffer controlled_buffer_7
endmodule

module KMOPR (
  input  HALT,
  input  RTS,
  input  RTI,
  input  PUSHPSW,
  input  POPPSW,
  input  PUSH,
  input  POP,
  input  INTE,
  input  INTD,
  input  BOVF,
  input  BNEQ,
  input  BLEQU,
  input  JLSS,
  input  JLEQ,
  input  JMP,
  input  LD,
  input  ST,
  input  JSR,
  input  TST,
  input  XOR,
  input  STRLEN,
  input  ADD,
  output [7:0] Adr7__0
);

  assign Adr7__0 = HALT ? 8'h2 : 8'bz;  // Controlled_Buffer controlled_buffer_1
  assign Adr7__0 = RTS ? 8'h3 : 8'bz;  // Controlled_Buffer controlled_buffer_2
  assign Adr7__0 = RTI ? 8'ha : 8'bz;  // Controlled_Buffer controlled_buffer_3
  assign Adr7__0 = PUSHPSW ? 8'h1f : 8'bz;  // Controlled_Buffer controlled_buffer_4
  assign Adr7__0 = POPPSW ? 8'h26 : 8'bz;  // Controlled_Buffer controlled_buffer_5
  assign Adr7__0 = PUSH ? 8'h2d : 8'bz;  // Controlled_Buffer controlled_buffer_6
  assign Adr7__0 = POP ? 8'h34 : 8'bz;  // Controlled_Buffer controlled_buffer_7
  assign Adr7__0 = INTD ? 8'h3d : 8'bz;  // Controlled_Buffer controlled_buffer_8
  assign Adr7__0 = INTE ? 8'h3c : 8'bz;  // Controlled_Buffer controlled_buffer_9
  assign Adr7__0 = BOVF ? 8'h3e : 8'bz;  // Controlled_Buffer controlled_buffer_10
  assign Adr7__0 = BNEQ ? 8'h3e : 8'bz;  // Controlled_Buffer controlled_buffer_11
  assign Adr7__0 = BLEQU ? 8'h3e : 8'bz;  // Controlled_Buffer controlled_buffer_12
  assign Adr7__0 = JLSS ? 8'h40 : 8'bz;  // Controlled_Buffer controlled_buffer_13
  assign Adr7__0 = JLEQ ? 8'h40 : 8'bz;  // Controlled_Buffer controlled_buffer_14
  assign Adr7__0 = JMP ? 8'h41 : 8'bz;  // Controlled_Buffer controlled_buffer_15
  assign Adr7__0 = LD ? 8'h42 : 8'bz;  // Controlled_Buffer controlled_buffer_16
  assign Adr7__0 = JSR ? 8'h4b : 8'bz;  // Controlled_Buffer controlled_buffer_17
  assign Adr7__0 = ST ? 8'h44 : 8'bz;  // Controlled_Buffer controlled_buffer_18
  assign Adr7__0 = TST ? 8'h53 : 8'bz;  // Controlled_Buffer controlled_buffer_19
  assign Adr7__0 = XOR ? 8'h54 : 8'bz;  // Controlled_Buffer controlled_buffer_20
  assign Adr7__0 = STRLEN ? 8'h56 : 8'bz;  // Controlled_Buffer controlled_buffer_21
  assign Adr7__0 = ADD ? 8'h5b : 8'bz;  // Controlled_Buffer controlled_buffer_22
endmodule

module PCD8 (
  input  En,
  input  C7,
  input  C6,
  input  C5,
  input  C4,
  input  C3,
  input  C2,
  input  C1,
  input  C0,
  output Z2,
  output Z1,
  output Z0,
  output W
);

  wire and_1_out, and_2_out, and_3_out, and_4_out, and_5_out, or_1_out, or_2_out, or_3_out, or_4_out;

  Pull_Resistor #(.pull(1)) pull_resistor_1 (.node(En));
  or or_1 (or_1_out, C7, C6, C5, C4, C3, C2, C1, C0);
  and and_1 (and_1_out, C2, ~C4, ~C5);  // AND_Gate
  and and_2 (and_2_out, C3, ~C4, ~C5);  // AND_Gate
  and and_3 (and_3_out, C1, ~C2, ~C4, ~C6);  // AND_Gate
  and and_4 (and_4_out, C4, ~C4, ~C6);  // AND_Gate
  and and_5 (and_5_out, C5, ~C6);  // AND_Gate
  or or_2 (or_2_out, C4, C5, C6, C7);
  or or_3 (or_3_out, and_1_out, and_2_out, C6, C7);
  or or_4 (or_4_out, and_3_out, and_4_out, and_5_out, C7);
  and and_6 (Z2, En, or_2_out);
  and and_7 (Z1, En, or_3_out);
  and and_8 (Z0, En, or_4_out);
  and and_9 (W, En, or_1_out);

  // Notes on the sheet:
  //   uezti za podrazumevanu vrednost logičku jedinicu
  //   Ako En nije priključen (stanje visoke impednase - HiZ),
endmodule

module REG5_INC_LD (
  input  [4:0] I4__0,
  input  LD,
  input  INC,
  input  mr,
  input  CLK,
  output [4:0] A4__0
);

  wire reg2m_inc_ld_1_p7, reg2m_inc_ld_2_p8;

  // REG2m_INC_LD reg2m_inc_ld_1: pin names not known; wires that end beside it: CLK, mr, I4__0[4:3], A4__0[4:3], LD, INC, reg2m_inc_ld_1_p7
  // REG2m_INC_LD reg2m_inc_ld_2: pin names not known; wires that end beside it: CLK, reg2m_inc_ld_1_p7, mr, I4__0[2:1], A4__0[2:1], LD, INC, reg2m_inc_ld_2_p8
  // REG1m_INC_LD reg1m_inc_ld_1: pin names not known; wires that end beside it: CLK, reg2m_inc_ld_2_p8, mr, I4__0[0], A4__0[0], LD, INC, INC

  // Notes on the sheet:
  //   __
endmodule

module REG6_INC_LD (
  input  [5:0] I5__0,
  input  LD,
  input  INC,
  input  mr,
  input  CLK,
  output [5:0] A5__0
);

  wire reg2m_inc_ld_1_p7, reg2m_inc_ld_2_p8;

  // REG2m_INC_LD reg2m_inc_ld_1: pin names not known; wires that end beside it: CLK, mr, I5__0[5:4], A5__0[5:4], LD, INC, reg2m_inc_ld_1_p7
  // REG2m_INC_LD reg2m_inc_ld_2: pin names not known; wires that end beside it: CLK, reg2m_inc_ld_1_p7, mr, I5__0[3:2], A5__0[3:2], LD, INC, reg2m_inc_ld_2_p8
  // REG2m_INC_LD reg2m_inc_ld_3: pin names not known; wires that end beside it: CLK, reg2m_inc_ld_2_p8, mr, I5__0[1:0], A5__0[1:0], LD, INC, INC

  // Notes on the sheet:
  //   __
endmodule

module REG7_INC_LD (
  input  [6:0] I6__0,
  input  LD,
  input  INC,
  input  mr,
  input  CLK,
  output [6:0] A6__0
);

  wire reg2m_inc_ld_1_p8, reg4m_inc_ld_1_p7;

  // REG4m_INC_LD reg4m_inc_ld_1: pin names not known; wires that end beside it: CLK, mr, I6__0[6:3], A6__0[6:3], LD, INC, reg4m_inc_ld_1_p7
  // REG2m_INC_LD reg2m_inc_ld_1: pin names not known; wires that end beside it: CLK, reg4m_inc_ld_1_p7, mr, I6__0[2:1], A6__0[2:1], LD, INC, reg2m_inc_ld_1_p8
  // REG1m_INC_LD reg1m_inc_ld_1: pin names not known; wires that end beside it: CLK, reg2m_inc_ld_1_p8, mr, I6__0[0], A6__0[0], LD, INC, INC

  // Notes on the sheet:
  //   __
endmodule

module REG32_LD (
  input  [31:0] I15__0,
  input  LD,
  input  mr,
  input  CLK,
  output [31:0] A15__0
);

  // REG16_LD reg16_ld_1: pin names not known; wires that end beside it: CLK, mr, I15__0[31:16], A15__0[31:16], LD
  // REG16_LD reg16_ld_2: pin names not known; wires that end beside it: CLK, mr, I15__0[15:0], A15__0[15:0], LD

  // Notes on the sheet:
  //   __
endmodule

module REG1m_DEC_INC_LD (
  input  Ii,
  input  LD,
  input  INC,
  input  Ci,
  input  DEC,
  input  Ei,
  input  CLK,
  input  mr,
  output Ai,
  output Cout,
  output Eout
);

  wire and_1_out, and_2_out, and_3_out, and_4_out, dff_1_p1, pull_resistor_1_node, pull_resistor_6_node,
       xor_1_out, xor_2_out;

  Pull_Resistor pull_resistor_1 (.node(pull_resistor_1_node));
  Pull_Resistor pull_resistor_2 (.node(Ei));
  Pull_Resistor pull_resistor_3 (.node(DEC));
  Pull_Resistor #(.pull(1)) pull_resistor_4 (.node(mr));
  Pull_Resistor pull_resistor_5 (.node(Ii));
  Pull_Resistor pull_resistor_6 (.node(pull_resistor_6_node));
  Pull_Resistor pull_resistor_7 (.node(INC));
  xor xor_1 (xor_1_out, Ci, Ai);
  xor xor_2 (xor_2_out, Ei, Ai);
  and and_1 (and_1_out, INC, xor_1_out);
  and and_2 (and_2_out, DEC, xor_2_out);
  and and_3 (and_3_out, Ii, LD);
  and and_4 (and_4_out, ~pull_resistor_6_node, ~INC, Ai);  // AND_Gate
  // DFF dff_1: pin names not known; wires that end beside it: dff_1_p1, CLK, mr, Ai
  or or_1 (dff_1_p1, and_3_out, and_4_out, and_1_out, and_2_out);
  and and_5 (Cout, Ai, pull_resistor_1_node);
  and and_6 (Eout, ~Ai, Ei);  // AND_Gate

  // Notes on the sheet:
  //   __
endmodule

module REG2m_DEC_INC_LD (
  input  [1:0] I1__0,
  input  LD,
  input  Cin,
  input  INC,
  input  Ein,
  input  DEC,
  input  mr,
  input  CLK,
  output Cout,
  output Eout,
  output [1:0] A1__0
);

  wire reg1m_dec_inc_ld_2_cout, reg1m_dec_inc_ld_2_eout;

  REG1m_DEC_INC_LD reg1m_dec_inc_ld_1 (
    .Ii(I1__0[1]), .LD(LD), .INC(INC), .Ci(reg1m_dec_inc_ld_2_cout), .DEC(DEC), .Ei(reg1m_dec_inc_ld_2_eout),
    .CLK(CLK), .mr(mr), .Ai(A1__0[1]), .Cout(Cout), .Eout(Eout));
  REG1m_DEC_INC_LD reg1m_dec_inc_ld_2 (
    .Ii(I1__0[0]), .LD(LD), .INC(INC), .Ci(Cin), .DEC(DEC), .Ei(Ein), .CLK(CLK), .mr(mr), .Ai(A1__0[0]),
    .Cout(reg1m_dec_inc_ld_2_cout), .Eout(reg1m_dec_inc_ld_2_eout));

  // Notes on the sheet:
  //   __
endmodule

module REG4m_DEC_INC_LD (
  input  [3:0] I3__0,
  input  LD,
  input  Cin,
  input  INC,
  input  Ein,
  input  DEC,
  input  mr,
  input  CLK,
  output Cout,
  output Eout,
  output [3:0] A3__0
);

  wire reg2m_dec_inc_ld_2_cout, reg2m_dec_inc_ld_2_eout;

  REG2m_DEC_INC_LD reg2m_dec_inc_ld_1 (
    .I1__0(I3__0[3:2]), .LD(LD), .Cin(reg2m_dec_inc_ld_2_cout), .INC(INC), .Ein(reg2m_dec_inc_ld_2_eout),
    .DEC(DEC), .mr(mr), .CLK(CLK), .Cout(Cout), .Eout(Eout), .A1__0(A3__0[3:2]));
  REG2m_DEC_INC_LD reg2m_dec_inc_ld_2 (
    .I1__0(I3__0[1:0]), .LD(LD), .Cin(Cin), .INC(INC), .Ein(Ein), .DEC(DEC), .mr(mr), .CLK(CLK),
    .Cout(reg2m_dec_inc_ld_2_cout), .Eout(reg2m_dec_inc_ld_2_eout), .A1__0(A3__0[1:0]));

  // Notes on the sheet:
  //   __
endmodule

module REG8m_DEC_INC_LD (
  input  [7:0] I7__0,
  input  LD,
  input  Cin,
  input  INC,
  input  Ein,
  input  DEC,
  input  mr,
  input  CLK,
  output Cout,
  output Eout,
  output [7:0] A7__0
);

  wire reg4m_dec_inc_ld_2_cout, reg4m_dec_inc_ld_2_eout;

  REG4m_DEC_INC_LD reg4m_dec_inc_ld_1 (
    .I3__0(I7__0[7:4]), .LD(LD), .Cin(reg4m_dec_inc_ld_2_cout), .INC(INC), .Ein(reg4m_dec_inc_ld_2_eout),
    .DEC(DEC), .mr(mr), .CLK(CLK), .Cout(Cout), .Eout(Eout), .A3__0(A7__0[7:4]));
  REG4m_DEC_INC_LD reg4m_dec_inc_ld_2 (
    .I3__0(I7__0[3:0]), .LD(LD), .Cin(Cin), .INC(INC), .Ein(Ein), .DEC(DEC), .mr(mr), .CLK(CLK),
    .Cout(reg4m_dec_inc_ld_2_cout), .Eout(reg4m_dec_inc_ld_2_eout), .A3__0(A7__0[3:0]));

  // Notes on the sheet:
  //   __
endmodule

module ROM32x20 (
  input  [4:0] A4__0,
  input  CS,
  output [19:0] DOUT
);

  ROM #(.addrWidth(5), .dataWidth(20)) rom_1 (.addr(A4__0), .data(DOUT), .sel(CS));
endmodule

module ROM32x28_ADDR (
  input  [4:0] A4__0,
  input  CS,
  output [27:0] DOUT
);

  ROM #(.addrWidth(5), .dataWidth(28)) rom_1 (.addr(A4__0), .data(DOUT), .sel(CS));
endmodule

module ROM32x28_INTR (
  input  [4:0] A4__0,
  input  CS,
  output [27:0] DOUT
);

  ROM #(.addrWidth(5), .dataWidth(28)) rom_1 (.addr(A4__0), .data(DOUT), .sel(CS));
endmodule

module ROM128x52 (
  input  [6:0] A6__0,
  input  CS,
  output [31:0] DOUT31__0,
  output [19:0] DOUT51__32
);

  ROM #(.addrWidth(7), .dataWidth(20)) rom_1 (.addr(A6__0), .data(DOUT51__32), .sel(CS));
  ROM #(.addrWidth(7), .dataWidth(32)) rom_2 (.addr(A6__0), .data(DOUT31__0), .sel(CS));
endmodule

module REGB (
);

  wire CLK, decB7__0, decB15__8, incB7__0, incB15__8, ldB7__0, ldB15__8, mxB0, mxB1, reg8m_dec_inc_ld_2_cout,
       reg8m_dec_inc_ld_2_eout;
  wire [7:0] B7__0, IR7__0, IR15__8, MDR7__0, mp4_8b_1_p5, mp4_8b_2_p5;
  wire [15:0] GPR15__0;
  wire [15:8] B15__0;

  // MP4_8b mp4_8b_1: pin names not known; wires that end beside it: mxB1, mxB0, MDR7__0, IR7__0, mp4_8b_1_p5, GPR15__0[15:8], 1'b1
  REG8m_DEC_INC_LD reg8m_dec_inc_ld_1 (
    .I7__0(mp4_8b_1_p5), .LD(ldB15__8), .Cin(reg8m_dec_inc_ld_2_cout), .INC(incB15__8),
    .Ein(reg8m_dec_inc_ld_2_eout), .DEC(decB15__8), .CLK(CLK), .A7__0(B15__0));  // open: mr, Cout, Eout
  // MP4_8b mp4_8b_2: pin names not known; wires that end beside it: mxB1, mxB0, MDR7__0, IR15__8, mp4_8b_2_p5, GPR15__0[7:0], 1'b1
  REG8m_DEC_INC_LD reg8m_dec_inc_ld_2 (
    .I7__0(mp4_8b_2_p5), .LD(ldB7__0), .Cin(incB7__0), .INC(incB7__0), .Ein(decB7__0), .DEC(decB7__0),
    .CLK(CLK), .Cout(reg8m_dec_inc_ld_2_cout), .Eout(reg8m_dec_inc_ld_2_eout), .A7__0(B7__0));  // open: mr

  // Other names for the same wires on the sheet: B15__0[7:0] = B7__0; B15__8[7:0] = B15__0
endmodule

module PSWV_ADD_SUB (
);

  wire A15, ADD, ALU15, and_1_out, and_2_out, and_3_out, and_4_out, and_5_out, and_6_out, and_7_out,
       and_8_out, and_9_out, B15, CLK, DW3, ldV, or_1_out, or_2_out, or_3_out, or_4_out, PSWV, rsff_1_p4,
       rst, RTI, SUB;

  and and_1 (and_1_out, ~ALU15, B15, A15);  // AND_Gate
  and and_2 (and_2_out, ALU15, ~B15, ~A15);  // AND_Gate
  and and_3 (and_3_out, ~ALU15, ~B15, A15);  // AND_Gate
  and and_4 (and_4_out, ALU15, B15, ~A15);  // AND_Gate
  or or_1 (or_1_out, and_1_out, and_2_out);
  or or_2 (or_2_out, and_3_out, and_4_out);
  and and_5 (and_5_out, DW3, RTI);
  and and_6 (and_6_out, ADD, or_1_out);
  or or_3 (or_3_out, and_6_out, and_7_out);
  and and_7 (and_7_out, SUB, or_2_out);
  or or_4 (or_4_out, and_5_out, or_3_out);
  and and_8 (and_8_out, ~or_4_out, ldV);  // AND_Gate
  and and_9 (and_9_out, or_4_out, ldV);
  // RSFF rsff_1: pin names not known; wires that end beside it: and_8_out, CLK, and_9_out, rsff_1_p4, PSWV
  not not_1 (rsff_1_p4, rst);
endmodule

module PSWC (
);

  wire ADD, and_1_out, and_2_out, and_3_out, and_4_out, C16, CLK, DW4, ldV, or_1_out, or_2_out, or_3_out,
       POPPSW, PSWV, rsff_1_p3, rsff_1_p4, rst, RTI, undriven, undriven_2;

  or or_1 (or_1_out, RTI, POPPSW);
  and and_1 (and_1_out, ADD, C16);
  and and_2 (and_2_out, undriven, undriven_2);
  and and_3 (and_3_out, or_1_out, DW4);
  or or_2 (or_2_out, and_1_out, and_2_out);
  or or_3 (or_3_out, and_3_out, or_2_out);
  and and_4 (and_4_out, ~or_3_out, ldV);  // AND_Gate
  // RSFF rsff_1: pin names not known; wires that end beside it: and_4_out, CLK, rsff_1_p3, rsff_1_p4, PSWV
  not not_1 (rsff_1_p4, rst);
  and and_5 (rsff_1_p3, or_3_out, ldV);
endmodule
