// Logisim project ORT2Project.circ as structural Verilog: 8 circuits, main circuit COMPUTER
module COMPUTER (
);

  wire BTN_RST_out, CLK, cpu_1_inta, interrupt_interface_8_1_p4, interrupt_interface_8_1_p5,
       interrupt_interface_8_1_p6, interrupt_interface_8_1_p7, interrupt_interface_8_1_p8,
       interrupt_interface_8_1_p9, interrupt_interface_8_1_p10, interrupt_interface_8_1_p11,
       pull_resistor_4_node, pull_resistor_6_node, ram_1_out_8, rst;
  wire [2:0] cpu_1_uext2__0;
  wire [7:0] interrupt_interface_8_1_p1, pull_resistor_1_node, ram_1_out_7;
  wire [15:0] pull_resistor_3_node;

  Button BTN_RST (.out(BTN_RST_out));
  Clock u_CLK (.out(CLK));
  // RisingEdge risingedge_1: pin names not known; wires that end beside it: BTN_RST_out, CLK, rst
  RAM ram_1 (
    .in_1(pull_resistor_3_node), .in_2(CLK), .in_3(pull_resistor_1_node), .in_4(pull_resistor_4_node),
    .in_5(pull_resistor_6_node), .in_6(rst), .out_7(ram_1_out_7), .out_8(ram_1_out_8));
  Pull_Resistor pull_resistor_1 (.node(pull_resistor_1_node));
  Pull_Resistor pull_resistor_2 (.node(ram_1_out_7));
  Pull_Resistor pull_resistor_3 (.node(pull_resistor_3_node));
  Pull_Resistor pull_resistor_4 (.node(pull_resistor_4_node));
  Pull_Resistor pull_resistor_5 (.node(ram_1_out_8));
  Pull_Resistor pull_resistor_6 (.node(pull_resistor_6_node));
  CPU cpu_1 (
    .in_1(rst), .in_2(CLK), .in_3(ram_1_out_8), .in_4(ram_1_out_7), .ABUS(pull_resistor_3_node),
    .DOUTBUS(pull_resistor_1_node), .out_8(pull_resistor_4_node), .out_9(pull_resistor_6_node),
    .inta(cpu_1_inta), .intr7__0(interrupt_interface_8_1_p1), .UEXT2__0(cpu_1_uext2__0));
  // INTERRUPT_INTERFACE_8 interrupt_interface_8_1: pin names not known; wires that end beside it: interrupt_interface_8_1_p1, cpu_1_inta, cpu_1_uext2__0, interrupt_interface_8_1_p4, interrupt_interface_8_1_p5, interrupt_interface_8_1_p6, interrupt_interface_8_1_p7, interrupt_interface_8_1_p8, interrupt_interface_8_1_p9, interrupt_interface_8_1_p10, interrupt_interface_8_1_p11, CLK
  Button BTN_INTR7 (.out(interrupt_interface_8_1_p4));
  Button BTN_INTR6 (.out(interrupt_interface_8_1_p5));
  Button BTN_INTR5 (.out(interrupt_interface_8_1_p6));
  Button BTN_INTR4 (.out(interrupt_interface_8_1_p7));
  Button BTN_INTR3 (.out(interrupt_interface_8_1_p8));
  Button BTN_INTR2 (.out(interrupt_interface_8_1_p9));
  Button BTN_INTR1 (.out(interrupt_interface_8_1_p10));
  Button BTN_INTR0 (.out(interrupt_interface_8_1_p11));
endmodule

module CPU (
  input  in_1,
  input  in_2,
  input  in_3,
  input  [7:0] in_4,
  input  [7:0] intr7__0,
  output [15:0] ABUS,
  output [7:0] DOUTBUS,
  output out_8,
  output out_9,
  output inta,
  output [2:0] UEXT2__0
);

  wire C16;
  wire [1:0] common_1_grbus;
  wire [3:0] common_1_phaseffbus;
  wire [7:0] common_1_addrbus, pull_resistor_6_node;
  wire [9:0] pull_resistor_1_node;
  wire [15:0] A, ALU, B, DW, INTRADDR, PSW;
  wire [23:0] common_1_instrucbus, pull_resistor_5_node, pull_resistor_7_node;

  COMMON common_1 (
    .CLK(in_2), .RST(in_1), .DIN(in_4), .CMEMBUS(pull_resistor_5_node), .MAR(ABUS), .MDR(DOUTBUS),
    .PHASEFFBUS(common_1_phaseffbus), .INSTRUCBUS(common_1_instrucbus), .ADDRBUS(common_1_addrbus),
    .PSW(PSW), .CREGBUS(pull_resistor_7_node), .CFFBUS(pull_resistor_6_node), .B(B), .A(A),
    .CPSW(pull_resistor_1_node), .ALU(ALU), .IVTPPDSP(INTRADDR), .GRBUS(common_1_grbus), .DW(DW), .C16(C16));
  Pull_Resistor pull_resistor_1 (.node(pull_resistor_1_node));
  Pull_Resistor pull_resistor_2 (.node(common_1_instrucbus));
  Pull_Resistor pull_resistor_3 (.node(common_1_phaseffbus));
  Pull_Resistor pull_resistor_4 (.node(common_1_addrbus));
  Pull_Resistor pull_resistor_5 (.node(pull_resistor_5_node));
  Pull_Resistor pull_resistor_6 (.node(pull_resistor_6_node));
  Pull_Resistor pull_resistor_7 (.node(pull_resistor_7_node));
  Pull_Resistor pull_resistor_8 (.node(common_1_grbus));
  FETCH fetch_1 (
    .in_1(in_1), .in_2(in_2), .in_3(in_3), .PHASEFFBUS(common_1_phaseffbus),
    .INSTRUCBUS(common_1_instrucbus), .ADDRBUS(common_1_addrbus), .PSW(PSW), .rdMEM(out_9),
    .CMEMBUS(pull_resistor_5_node), .CFFBUS(pull_resistor_6_node), .CREGBUS(pull_resistor_7_node),
    .GRBUS(common_1_grbus));
  ADDR addr_1 (
    .rdMEM(out_9), .CMEMBUS(pull_resistor_5_node), .CFFBUS(pull_resistor_6_node),
    .CREGBUS(pull_resistor_7_node), .in_1(in_1), .in_2(in_2), .in_3(in_3), .PHASEFFBUS(common_1_phaseffbus),
    .INSTRUCBUS(common_1_instrucbus), .ADDRBUS(common_1_addrbus));
  EXEC exec_1 (
    .B(B), .A(A), .ALU(ALU), .CMEMBUS(pull_resistor_5_node), .CFFBUS(pull_resistor_6_node),
    .CREGBUS(pull_resistor_7_node), .CPSW(pull_resistor_1_node), .rdMEM(out_9), .wrMEM(out_8), .in_1(in_1),
    .in_2(in_2), .in_3(in_3), .PHASEFFBUS(common_1_phaseffbus), .INSTRUCBUS(common_1_instrucbus), .PSW(PSW),
    .ADDRBUS(common_1_addrbus), .DW(DW), .C16(C16), .MDR(DOUTBUS));
  INTR intr_1 (
    .intr(intr7__0), .ADDIVTP(INTRADDR), .CMEMBUS(pull_resistor_5_node), .CFFBUS(pull_resistor_6_node),
    .CREGBUS(pull_resistor_7_node), .rdMEM(out_9), .wrMEM(out_8), .UEXT2__0(UEXT2__0), .inta(inta),
    .in_1(in_1), .in_2(in_2), .in_3(in_3), .PHASEFFBUS(common_1_phaseffbus),
    .INSTRUCBUS(common_1_instrucbus), .PSW(PSW));

  // Other names for the same wires on the sheet: CLK = in_2; DIN7__0[7:0] = in_4; FCBUS = in_3; MAR[15:0] = ABUS;
  //   MDR[7:0] = DOUTBUS; RD = out_9; rst = in_1; WR = out_8
endmodule

module COMMON (
  input  CLK,
  input  RST,
  input  [7:0] DIN,
  input  [15:0] A,
  input  [15:0] ALU,
  input  C16,
  input  [15:0] IVTPPDSP,
  input  [23:0] CMEMBUS,
  input  [7:0] CFFBUS,
  input  [23:0] CREGBUS,
  input  [9:0] CPSW,
  output [15:0] MAR,
  output [7:0] MDR,
  output [3:0] PHASEFFBUS,
  output [23:0] INSTRUCBUS,
  output [7:0] ADDRBUS,
  output [1:0] GRBUS,
  output [15:0] PSW,
  output [15:0] B,
  output [15:0] DW
);

  wire adres7, adres8, adres9, adres10, adres11, adres12, adres13, adres14, adres15, ADRINST, adrinstr,
       and_1_out, and_2_out, and_3_out, and_4_out, and_5_out, and_6_out, and_7_out, and_8_out, and_9_out,
       and_10_out, and_11_out, and_12_out, and_13_out, and_14_out, and_15_out, and_16_out, and_17_out,
       and_18_out, and_19_out, and_20_out, and_21_out, and_22_out, and_24_out, and_26_out, and_28_out,
       and_30_out, bezadrinstr, branchinstr, grupa4, grupa5, grupa6, grupa7, grupa8, grupa9, grupa10,
       grupa11, grupa12, grupa13, grupa14, grupa15, instr09, instr010, instr011, instr012, instr013,
       instr014, instr015, instr15, instr16, instr17, instr18, instr19, instr21, instr22, instr23, instr24,
       instr25, instr26, instr27, instr28, instr29, instr37, instr38, instr39, instr110, instr111, instr112,
       instr113, instr114, instr115, instr210, instr211, instr212, instr213, instr214, instr215, instr310,
       instr311, instr312, instr313, instr314, instr315, jmpinstr, mp2_8b_1_p3, mp2_8b_2_p3, mp2_16b_1_p3,
       mp2_16b_2_p3, mp4_16b_1_p5, mp4_16b_2_p5, mp8_8b_1_p8, mp8_16b_1_p8, not_1_out, not_5_out, not_10_out,
       or_1_out, or_2_out, or_6_out, or_7_out, or_8_out, or_9_out, or_10_out, or_11_out, or_12_out,
       or_13_out, or_14_out, or_15_out, or_16_out, or_17_out, or_18_out, or_19_out, or_20_out, or_21_out,
       or_23_out, reg16_inc_ld_2_p4, rsff_2_p4, rsff_3_p4, rsff_4_p4, rsff_6_p3, rsff_6_p4, rsff_7_p3,
       rsff_7_p4, rsff_8_p3, rsff_8_p4, rsff_9_p3, rsff_9_p4, rsff_10_p3, rsff_10_p5;
  wire [3:0] IR27__24;
  wire [7:0] IR7__0, IR15__8, IR23__16;
  wire [7:4] IR31__24;
  wire [15:0] ADDPCREL15__0, ADDW15__0, GPR15__0, PC15__0, SP15__0;

  // MP8_16b mp8_16b_1: pin names not known; wires that end beside it: CMEMBUS[7], CMEMBUS[6], CMEMBUS[5], PC15__0, {IR7__0, IR15__8}, ADDW15__0, DW, mp8_16b_1_p8, B, GPR15__0, SP15__0, IVTPPDSP, 1'b1
  // REG16_INC_LD reg16_inc_ld_1: pin names not known; wires that end beside it: CLK, mp8_16b_1_p8, MAR, CMEMBUS[0], CMEMBUS[1]
  // REG8_LD reg8_ld_1: pin names not known; wires that end beside it: CLK, MDR, {IR31__24, IR27__24}, CREGBUS[3]
  // REG8_LD reg8_ld_2: pin names not known; wires that end beside it: CLK, MDR, IR15__8, CREGBUS[1]
  Decoder #(.select(4), .disabled(0)) decoder_1 (
    .out0(bezadrinstr), .out1(branchinstr), .out2(jmpinstr), .out3(adrinstr), .out4(grupa4), .out5(grupa5),
    .out6(grupa6), .out7(grupa7), .out8(grupa8), .out9(grupa9), .out10(grupa10), .out11(grupa11),
    .out12(grupa12), .out13(grupa13), .out14(grupa14), .out15(grupa15), .sel(IR31__24), .en(PSW[0]));
  Decoder #(.select(4), .disabled(0)) decoder_2 (
    .out0(INSTRUCBUS[14]), .out1(instr21), .out2(instr22), .out3(instr23), .out4(instr24), .out5(instr25),
    .out6(instr26), .out7(instr27), .out8(instr28), .out9(instr29), .out10(instr210), .out11(instr211),
    .out12(instr212), .out13(instr213), .out14(instr214), .out15(instr215), .sel(IR27__24), .en(jmpinstr));
  // ADD16 add16_1: pin names not known; wires that end beside it: {{9{IR15__8[7]}}, IR15__8[6:0]}, ADDW15__0, GPR15__0
  // MP4_16b mp4_16b_1: pin names not known; wires that end beside it: CREGBUS[6], CREGBUS[5], DW, {IR7__0, IR15__8}, mp4_16b_1_p5, GPR15__0, 1'b1
  // REG16 reg16_1: pin names not known; wires that end beside it: CLK, mp4_16b_1_p5, B, CREGBUS[4], CREGBUS[7], CREGBUS[8]
  or or_1 (or_1_out, grupa4, grupa5, grupa6, grupa7, grupa8, grupa9, grupa10, grupa11, grupa12, grupa13, grupa14, grupa15, instr09, instr010, instr011, instr012, instr013, instr014, instr015, instr15, instr16, instr17, instr18, instr19, instr110, instr111, instr112);
  // MP8_8b mp8_8b_1: pin names not known; wires that end beside it: CMEMBUS[10], CMEMBUS[9], CMEMBUS[8], DIN, A[7:0], A[15:8], PC15__0[15:8], mp8_8b_1_p8, PC15__0[7:0], {PSW[15], {7{1'b0}}}, {3'b000, PSW[4:0]}, 1'b1
  // REG8_LD reg8_ld_3: pin names not known; wires that end beside it: CLK, mp8_8b_1_p8, MDR, CMEMBUS[2]
  // REG8_LD reg8_ld_4: pin names not known; wires that end beside it: CLK, MDR, IR23__16, CREGBUS[2]
  // REG8_LD reg8_ld_5: pin names not known; wires that end beside it: CLK, MDR, IR7__0, CREGBUS[0]
  Decoder #(.select(4), .disabled(0)) decoder_3 (
    .out0(INSTRUCBUS[0]), .out1(INSTRUCBUS[1]), .out2(INSTRUCBUS[2]), .out3(INSTRUCBUS[3]),
    .out4(INSTRUCBUS[4]), .out5(INSTRUCBUS[5]), .out6(INSTRUCBUS[6]), .out7(INSTRUCBUS[7]),
    .out8(INSTRUCBUS[8]), .out9(instr09), .out10(instr010), .out11(instr011), .out12(instr012),
    .out13(instr013), .out14(instr014), .out15(instr015), .sel(IR27__24), .en(bezadrinstr));
  Decoder #(.select(4), .disabled(0)) decoder_4 (
    .out0(INSTRUCBUS[15]), .out1(INSTRUCBUS[16]), .out2(INSTRUCBUS[17]), .out3(INSTRUCBUS[18]),
    .out4(INSTRUCBUS[19]), .out5(INSTRUCBUS[20]), .out6(INSTRUCBUS[21]), .out7(instr37), .out8(instr38),
    .out9(instr39), .out10(instr310), .out11(instr311), .out12(instr312), .out13(instr313), .out14(instr314),
    .out15(instr315), .sel(IR27__24), .en(adrinstr));
  // ADD16 add16_2: pin names not known; wires that end beside it: {{9{IR23__16[7]}}, IR23__16[6:0]}, ADDPCREL15__0, PC15__0
  or or_2 (or_2_out, adres15, adres14, adres13, adres12, adres11, adres10, adres9, adres8, adres7);
  // MP2_8b mp2_8b_1: pin names not known; wires that end beside it: CREGBUS[13], MDR, mp2_8b_1_p3, MAR[15:8], 1'b1
  // REG8_LD reg8_ld_6: pin names not known; wires that end beside it: CLK, mp2_8b_1_p3, DW[15:8], CREGBUS[11]
  and and_1 (and_1_out, adrinstr, or_2_out);
  Decoder #(.select(4), .disabled(0)) decoder_5 (
    .out0(INSTRUCBUS[9]), .out1(INSTRUCBUS[10]), .out2(INSTRUCBUS[11]), .out3(INSTRUCBUS[12]),
    .out4(INSTRUCBUS[13]), .out5(instr15), .out6(instr16), .out7(instr17), .out8(instr18), .out9(instr19),
    .out10(instr110), .out11(instr111), .out12(instr112), .out13(instr113), .out14(instr114),
    .out15(instr115), .sel(IR27__24), .en(branchinstr));
  Decoder #(.select(4), .disabled(0)) decoder_6 (
    .out0(ADDRBUS[0]), .out1(ADDRBUS[1]), .out2(ADDRBUS[2]), .out3(ADDRBUS[3]), .out4(ADDRBUS[4]),
    .out5(ADDRBUS[5]), .out6(ADDRBUS[6]), .out7(adres7), .out8(adres8), .out9(adres9), .out10(adres10),
    .out11(adres11), .out12(adres12), .out13(adres13), .out14(adres14), .out15(adres15), .sel(IR23__16[7:4]),
    .en(adrinstr));
  not not_1 (not_1_out, RST);
  // RSFF rsff_1: pin names not known; wires that end beside it: CFFBUS[1], CLK, CFFBUS[0], not_1_out, PHASEFFBUS[0]
  // MP4_16b mp4_16b_2: pin names not known; wires that end beside it: CMEMBUS[12], CMEMBUS[11], {IR7__0, IR15__8}, ADDPCREL15__0, mp4_16b_2_p5, DW, {IR15__8, IR23__16}, 1'b1
  // MP2_16b mp2_16b_1: pin names not known; wires that end beside it: RST, mp4_16b_2_p5, mp2_16b_1_p3, 16'h1000, 1'b1
  // REG16_INC_LD reg16_inc_ld_2: pin names not known; wires that end beside it: CLK, mp2_16b_1_p3, PC15__0, reg16_inc_ld_2_p4, CMEMBUS[4]
  // MP2_8b mp2_8b_2: pin names not known; wires that end beside it: CREGBUS[13], MDR, mp2_8b_2_p3, MAR[7:0], 1'b1
  // REG8_LD reg8_ld_7: pin names not known; wires that end beside it: CLK, mp2_8b_2_p3, DW[7:0], CREGBUS[10]
  // REG16 reg16_2: pin names not known; wires that end beside it: CLK, 16'hf000, SP15__0, RST, CMEMBUS[13], CMEMBUS[14]
  or or_3 (GRBUS[0], or_1_out, or_14_out);
  or or_4 (GRBUS[1], and_1_out, or_6_out);
  or or_5 (reg16_inc_ld_2_p4, CMEMBUS[3], RST);
  or or_6 (or_6_out, and_2_out, and_3_out, and_4_out);
  // RSFF rsff_2: pin names not known; wires that end beside it: CFFBUS[3], CLK, CFFBUS[2], rsff_2_p4, PHASEFFBUS[1]
  not not_2 (rsff_2_p4, RST);
  and and_2 (and_2_out, or_7_out, INSTRUCBUS[17]);
  and and_3 (and_3_out, ADDRBUS[0], INSTRUCBUS[16]);
  and and_4 (and_4_out, INSTRUCBUS[20], or_8_out);
  or or_7 (or_7_out, ADDRBUS[0], ADDRBUS[2]);
  or or_8 (or_8_out, ADDRBUS[0], ADDRBUS[2]);
  or or_9 (or_9_out, INSTRUCBUS[2], INSTRUCBUS[4]);
  or or_10 (or_10_out, INSTRUCBUS[2], INSTRUCBUS[4]);
  or or_11 (or_11_out, INSTRUCBUS[2], INSTRUCBUS[4]);
  and and_5 (and_5_out, ~ALU[15], B[15], A[15]);  // AND_Gate
  or or_12 (or_12_out, and_5_out, and_6_out);
  and and_6 (and_6_out, ALU[15], ~B[15], ~A[15]);  // AND_Gate
  or or_13 (or_13_out, INSTRUCBUS[2], INSTRUCBUS[4]);
  and and_7 (and_7_out, INSTRUCBUS[21], C16);
  or or_14 (or_14_out, instr113, instr114, instr115, instr21, instr22, instr23, instr24, instr25, instr26, instr27, instr28, instr29, instr210, instr211, instr212, instr213, instr214, instr215, instr37, instr38, instr39, instr310, instr311, instr312, instr313, instr314, instr315);
  // RSFF rsff_3: pin names not known; wires that end beside it: CFFBUS[5], CLK, CFFBUS[4], rsff_3_p4, PHASEFFBUS[2]
  not not_3 (rsff_3_p4, RST);
  or or_15 (or_15_out, INSTRUCBUS[2], INSTRUCBUS[4]);
  and and_8 (and_8_out, or_9_out, DW[1]);
  and and_9 (and_9_out, ADRINST, and_10_out);
  and and_10 (and_10_out, ~A[0], ~A[1], ~A[2], ~A[3], ~A[4], ~A[5], ~A[6], ~A[7], ~A[8], ~A[9], ~A[10], ~A[11], ~A[12], ~A[13], ~A[14], ~A[15]);  // AND_Gate
  and and_11 (and_11_out, INSTRUCBUS[18], and_12_out);
  and and_12 (and_12_out, ~ALU[0], ~ALU[1], ~ALU[2], ~ALU[3], ~ALU[4], ~ALU[5], ~ALU[6], ~ALU[7], ~ALU[8], ~ALU[9], ~ALU[10], ~ALU[11], ~ALU[12], ~ALU[13], ~ALU[14], ~ALU[15]);  // AND_Gate
  and and_13 (and_13_out, or_10_out, DW[2]);
  and and_14 (and_14_out, ADRINST, A[15]);
  and and_15 (and_15_out, INSTRUCBUS[18], ALU[15]);
  and and_16 (and_16_out, or_11_out, DW[3]);
  and and_17 (and_17_out, INSTRUCBUS[21], or_12_out);
  and and_18 (and_18_out, or_13_out, DW[4]);
  or or_16 (or_16_out, INSTRUCBUS[2], INSTRUCBUS[4]);
  and and_19 (and_19_out, or_15_out, ~DW[0], CPSW[6]);  // AND_Gate
  and and_20 (and_20_out, or_15_out, DW[0], CPSW[6]);
  or or_17 (or_17_out, and_8_out, and_9_out, and_11_out);
  or or_18 (or_18_out, and_13_out, and_14_out, and_15_out);
  or or_19 (or_19_out, and_16_out, and_17_out);
  or or_20 (or_20_out, and_18_out, and_7_out);
  and and_21 (and_21_out, or_16_out, DW[15]);
  // MP2_16b mp2_16b_2: pin names not known; wires that end beside it: CREGBUS[12], B, mp2_16b_2_p3, A, 1'b1
  // GPR8x16 gpr8x16_1: pin names not known; wires that end beside it: IR23__16[3:1], CLK, mp2_16b_2_p3, GPR15__0, CREGBUS[9]
  or or_21 (or_21_out, and_19_out, CPSW[0]);
  // RSFF rsff_4: pin names not known; wires that end beside it: CFFBUS[7], CLK, CFFBUS[6], rsff_4_p4, PHASEFFBUS[3]
  not not_4 (rsff_4_p4, RST);
  not not_5 (not_5_out, RST);
  // RSFF rsff_5: pin names not known; wires that end beside it: or_21_out, CLK, and_20_out, not_5_out, PSW[0]
  and and_22 (and_22_out, ~or_17_out, CPSW[5]);  // AND_Gate
  // RSFF rsff_6: pin names not known; wires that end beside it: and_22_out, CLK, rsff_6_p3, rsff_6_p4, PSW[1]
  and and_23 (rsff_6_p3, or_17_out, CPSW[5]);
  not not_6 (rsff_6_p4, RST);
  or or_22 (ADRINST, INSTRUCBUS[6], INSTRUCBUS[15], INSTRUCBUS[19], INSTRUCBUS[20], INSTRUCBUS[21]);
  and and_24 (and_24_out, ~or_18_out, CPSW[4]);  // AND_Gate
  // RSFF rsff_7: pin names not known; wires that end beside it: and_24_out, CLK, rsff_7_p3, rsff_7_p4, PSW[2]
  not not_7 (rsff_7_p4, RST);
  and and_25 (rsff_7_p3, or_18_out, CPSW[4]);
  and and_26 (and_26_out, ~or_19_out, CPSW[3]);  // AND_Gate
  // RSFF rsff_8: pin names not known; wires that end beside it: and_26_out, CLK, rsff_8_p3, rsff_8_p4, PSW[3]
  not not_8 (rsff_8_p4, RST);
  and and_27 (rsff_8_p3, or_19_out, CPSW[3]);
  and and_28 (and_28_out, ~or_20_out, CPSW[2]);  // AND_Gate
  // RSFF rsff_9: pin names not known; wires that end beside it: and_28_out, CLK, rsff_9_p3, rsff_9_p4, PSW[4]
  not not_9 (rsff_9_p4, RST);
  and and_29 (rsff_9_p3, or_20_out, CPSW[2]);
  or or_23 (or_23_out, RST, CPSW[7]);
  not not_10 (not_10_out, or_23_out);
  and and_30 (and_30_out, ~and_21_out, CPSW[1]);  // AND_Gate
  // RSFF rsff_10: pin names not known; wires that end beside it: and_30_out, CLK, rsff_10_p3, not_10_out, rsff_10_p5, PSW[15]
  not not_11 (rsff_10_p5, CPSW[8]);
  and and_31 (rsff_10_p3, and_21_out, CPSW[1]);

  assign PSW[14:5] = {10{1'b0}};

  // Other names for the same wires on the sheet: A7__0[7:0] = A[7:0]; A15__0[15:0] = A; A15__8[7:0] = A[15:8];
  //   immed = ADDRBUS[0]; memdir = ADDRBUS[1]; regdir = ADDRBUS[2]; memind = ADDRBUS[3]; preincr = ADDRBUS[4];
  //   postdec = ADDRBUS[5]; regindpom = ADDRBUS[6]; ALU15__0[15:0] = ALU; B15__0[15:0] = B; stFETCH = CFFBUS[0];
  //   clFETCH = CFFBUS[1]; stADDR = CFFBUS[2]; clADDR = CFFBUS[3]; stEXEC = CFFBUS[4]; clEXEC = CFFBUS[5];
  //   stINTR = CFFBUS[6]; clINTR = CFFBUS[7]; ldMAR = CMEMBUS[0]; incMAR = CMEMBUS[1]; ldMDR = CMEMBUS[2];
  //   ldPC = CMEMBUS[3]; incPC = CMEMBUS[4]; mxMAR0 = CMEMBUS[5]; mxMAR1 = CMEMBUS[6]; mxMAR2 = CMEMBUS[7];
  //   mxMDR0 = CMEMBUS[8]; mxMDR1 = CMEMBUS[9]; mxMDR2 = CMEMBUS[10]; mxPC0 = CMEMBUS[11]; mxPC1 = CMEMBUS[12];
  //   incSP = CMEMBUS[13]; decSP = CMEMBUS[14]; clPSWSTART = CPSW[0]; ldI = CPSW[1]; ldC = CPSW[2]; ldV = CPSW[3];
  //   ldN = CPSW[4]; ldZ = CPSW[5]; ldSTART = CPSW[6]; stPSWI = CPSW[7]; clPSWI = CPSW[8]; ldIR7__0 = CREGBUS[0];
  //   ldIR15__8 = CREGBUS[1]; ldIR23__16 = CREGBUS[2]; ldIR31__24 = CREGBUS[3]; ldB = CREGBUS[4]; mxB0 = CREGBUS[5];
  //   mxB1 = CREGBUS[6]; incB = CREGBUS[7]; decB = CREGBUS[8]; wrGPR = CREGBUS[9]; ldDWL = CREGBUS[10];
  //   ldDWH = CREGBUS[11]; mxGPR = CREGBUS[12]; mxDW = CREGBUS[13]; Din7__0[7:0] = DIN; DW15__0[15:0] = DW;
  //   DWL7__0[7:0] = DW[7:0]; DWH7__0[7:0] = DW[15:8]; ENTRADDR15__0[15:0] = IVTPPDSP; grinst = GRBUS[0];
  //   gradr = GRBUS[1]; HALT = INSTRUCBUS[0]; RTS = INSTRUCBUS[1]; RTI = INSTRUCBUS[2]; PUSHPSW = INSTRUCBUS[3];
  //   POPPSW = INSTRUCBUS[4]; PUSH = INSTRUCBUS[5]; POP = INSTRUCBUS[6]; INTE = INSTRUCBUS[7]; INTD = INSTRUCBUS[8];
  //   BOVF = INSTRUCBUS[9]; BNEQ = INSTRUCBUS[10]; BLEQU = INSTRUCBUS[11]; JLSS = INSTRUCBUS[12];
  //   JLEQ = INSTRUCBUS[13]; JMP = INSTRUCBUS[14]; LD = INSTRUCBUS[15]; ST = INSTRUCBUS[16]; JSR = INSTRUCBUS[17];
  //   TST = INSTRUCBUS[18]; XOR = INSTRUCBUS[19]; STRLEN = INSTRUCBUS[20]; ADD = INSTRUCBUS[21];
  //   IR31__24[3:0] = IR27__24; MAR15__0[15:0] = MAR; MDR7__0[7:0] = MDR; FETCH = PHASEFFBUS[0]; ADDR = PHASEFFBUS[1];
  //   EXEC = PHASEFFBUS[2]; INTR = PHASEFFBUS[3]; PSW15__0 (some bits) = {PSW[15], PSW[4:0]}; PSWSTART = PSW[0];
  //   PSWZ = PSW[1]; PSWN = PSW[2]; PSWV = PSW[3]; PSWC = PSW[4]; PSWI = PSW[15]

  // Notes on the sheet:
  //   Sabirači
  //   Instrukcijski registar
  //   Pomoćni registri
  //   MAR
  //   Dekoderi za prepoznavanje instrukcije na osnovu sadrzaja registara IR31..24 i  IR23..16
  //   MDR
  //   SP
  //   PC
  //   FF za pokretanje FETCH, ADDR, EXEC i INTR faze izvršavanja instrukcije
  //   Registarski fajl
  //   Programska statusna reč (PSW)
endmodule

module FETCH (
  input  in_1,
  input  in_2,
  input  in_3,
  input  [3:0] PHASEFFBUS,
  input  [23:0] INSTRUCBUS,
  input  [7:0] ADDRBUS,
  input  [1:0] GRBUS,
  input  [15:0] PSW,
  output [23:0] CMEMBUS,
  output [7:0] CFFBUS,
  output [23:0] CREGBUS,
  output rdMEM
);

  wire adr, adr2, adr3, adr4, and_3_out, and_4_out, and_5_out, and_6_out, and_7_out, and_8_out, and_9_out,
       and_10_out, and_11_out, bezadr1, bradr2, bradr3, brbezadr1, brcnd, brgradr, brgrinst, brjmp2, brjmp3,
       brnotFCBUS, brnotPSWSTARTandFETCH, bruncnd, clFETCH, incPC, jmp2, jmp3, ldIR7__0, ldIR15__8,
       ldIR23__16, ldIR31__24, ldMAR, ldMDR, not_1_out, not_2_out, not_3_out, not_4_out, not_5_out, or_3_out,
       or_6_out, or_7_out, or_8_out, rdMEM_t, stADDR, stEXEC;
  wire [3:0] rom_1_data_3;
  wire [5:0] reg6_inc_ld_1_a5__0, rom_1_data;
  wire [13:11] rom_1_data_2;

  or or_1 (bezadr1, INSTRUCBUS[0], INSTRUCBUS[1], INSTRUCBUS[2], INSTRUCBUS[3], INSTRUCBUS[4], INSTRUCBUS[5], INSTRUCBUS[6], INSTRUCBUS[7], INSTRUCBUS[8]);
  or or_2 (jmp2, INSTRUCBUS[9], INSTRUCBUS[10], INSTRUCBUS[11]);
  not not_1 (not_1_out, in_1);
  REG6_INC_LD reg6_inc_ld_1 (
    .I5__0(rom_1_data), .LD(or_3_out), .INC(not_2_out), .mr(not_1_out), .CLK(in_2),
    .A5__0(reg6_inc_ld_1_a5__0));
  not not_2 (not_2_out, or_3_out);
  Decoder #(.select(4), .disabled(0)) decoder_1 (
    .out1(bruncnd), .out2(brnotPSWSTARTandFETCH), .out3(brbezadr1), .out4(brjmp2), .out5(bradr2),
    .out6(brjmp3), .out7(bradr3), .out8(brnotFCBUS), .out9(brgrinst), .out10(brgradr), .sel(rom_1_data_3),
    .en(1'b1));  // open: out0, out11, out12, out13, out14, out15
  or or_3 (or_3_out, bruncnd, brcnd);
  ROM #(.addrWidth(6), .dataWidth(24)) rom_1 (
    .addr(reg6_inc_ld_1_a5__0),
    .data({rom_1_data, rom_1_data_3, rom_1_data_2, stEXEC, stADDR, clFETCH, ldIR7__0, ldIR15__8, ldIR23__16, ldIR31__24, ldMDR, rdMEM_t, incPC, ldMAR}),
    .sel(1'b1));
  or or_4 (jmp3, INSTRUCBUS[12], INSTRUCBUS[13], INSTRUCBUS[14]);
  or or_5 (adr, INSTRUCBUS[15], INSTRUCBUS[16], INSTRUCBUS[17], INSTRUCBUS[18], INSTRUCBUS[19], INSTRUCBUS[20], INSTRUCBUS[21]);
  or or_6 (or_6_out, ADDRBUS[2], ADDRBUS[4], ADDRBUS[5]);
  not not_3 (not_3_out, PHASEFFBUS[0]);
  not not_4 (not_4_out, PSW[0]);
  and and_1 (adr2, or_6_out, adr);
  and and_2 (adr3, ADDRBUS[6], adr);
  or or_7 (or_7_out, not_3_out, not_4_out);
  not not_5 (not_5_out, in_3);
  and and_3 (and_3_out, or_7_out, brnotPSWSTARTandFETCH);
  and and_4 (and_4_out, brbezadr1, bezadr1);
  and and_5 (and_5_out, brjmp2, jmp2);
  and and_6 (and_6_out, bradr2, adr2);
  and and_7 (and_7_out, brjmp3, jmp3);
  and and_8 (and_8_out, bradr3, adr3);
  and and_9 (and_9_out, brnotFCBUS, not_5_out);
  and and_10 (and_10_out, brgrinst, GRBUS[0]);
  and and_11 (and_11_out, brgradr, GRBUS[1]);
  or or_8 (or_8_out, ADDRBUS[0], ADDRBUS[1], ADDRBUS[3]);
  or or_9 (brcnd, and_3_out, and_4_out, and_5_out, and_6_out, and_7_out, and_8_out, and_9_out, and_10_out, and_11_out);
  and and_12 (adr4, or_8_out, adr);
  assign CMEMBUS[0] = ldMAR ? 1'b1 : 1'bz;  // Controlled_Buffer controlled_buffer_1
  assign CMEMBUS[2] = ldMDR ? 1'b1 : 1'bz;  // Controlled_Buffer controlled_buffer_2
  assign CMEMBUS[4] = incPC ? 1'b1 : 1'bz;  // Controlled_Buffer controlled_buffer_3
  assign CFFBUS[1] = clFETCH ? 1'b1 : 1'bz;  // Controlled_Buffer controlled_buffer_4
  assign CFFBUS[2] = stADDR ? 1'b1 : 1'bz;  // Controlled_Buffer controlled_buffer_5
  assign CFFBUS[4] = stEXEC ? 1'b1 : 1'bz;  // Controlled_Buffer controlled_buffer_6
  assign CREGBUS[0] = ldIR7__0 ? 1'b1 : 1'bz;  // Controlled_Buffer controlled_buffer_7
  assign CREGBUS[1] = ldIR15__8 ? 1'b1 : 1'bz;  // Controlled_Buffer controlled_buffer_8
  assign CREGBUS[2] = ldIR23__16 ? 1'b1 : 1'bz;  // Controlled_Buffer controlled_buffer_9
  assign CREGBUS[3] = ldIR31__24 ? 1'b1 : 1'bz;  // Controlled_Buffer controlled_buffer_10
  assign rdMEM = rdMEM_t ? 1'b1 : 1'bz;  // Controlled_Buffer controlled_buffer_11

  // Other names for the same wires on the sheet: immed = ADDRBUS[0]; memdir = ADDRBUS[1]; regdir = ADDRBUS[2];
  //   memind = ADDRBUS[3]; preincr = ADDRBUS[4]; postdec = ADDRBUS[5]; regindpom = ADDRBUS[6]; CLK = in_2;
  //   FCBUS = in_3; grinst = GRBUS[0]; gradr = GRBUS[1]; HALT = INSTRUCBUS[0]; RTS = INSTRUCBUS[1];
  //   RTI = INSTRUCBUS[2]; PUSHPSW = INSTRUCBUS[3]; POPPSW = INSTRUCBUS[4]; PUSH = INSTRUCBUS[5]; POP = INSTRUCBUS[6];
  //   INTE = INSTRUCBUS[7]; INTD = INSTRUCBUS[8]; BOVF = INSTRUCBUS[9]; BNEQ = INSTRUCBUS[10]; BLEQU = INSTRUCBUS[11];
  //   JLSS = INSTRUCBUS[12]; JLEQ = INSTRUCBUS[13]; JMP = INSTRUCBUS[14]; LD = INSTRUCBUS[15]; ST = INSTRUCBUS[16];
  //   JSR = INSTRUCBUS[17]; TST = INSTRUCBUS[18]; XOR = INSTRUCBUS[19]; STRLEN = INSTRUCBUS[20]; ADD = INSTRUCBUS[21];
  //   FETCH = PHASEFFBUS[0]; ADDR = PHASEFFBUS[1]; EXEC = PHASEFFBUS[2]; INTR = PHASEFFBUS[3]; PSWSTART = PSW[0];
  //   rst = in_1

  // Notes on the sheet:
  //   Operaciona jedinica
  //   Kontrolna jedinica
  //   contents of rom_1 (hex, n*v repeats v):
  //   8000 3 a000c 10 24000 50c000 3 1e000c 20 28000 510000 4d4000 3 36000c 518040 4dc000 3 46000c 80 4300
  //   4500
endmodule

module ADDR (
  input  in_1,
  input  in_2,
  input  in_3,
  input  [3:0] PHASEFFBUS,
  input  [23:0] INSTRUCBUS,
  input  [7:0] ADDRBUS,
  output [23:0] CMEMBUS,
  output [7:0] CFFBUS,
  output [23:0] CREGBUS,
  output rdMEM
);

  wire and_1_out, and_2_out, and_3_out, bradr, brcnd, brnotADDR, brnotFCBUS, brSTOREorJSRorSTRLEN, bruncnd,
       clADDR, decB, incB, incMAR, ldB, ldDWH, ldDWL, ldMAR, ldMDR, mxB0, mxB1, mxMAR0, mxMAR1, mxMAR2,
       not_1_out, not_2_out, not_3_out, not_4_out, or_1_out, or_2_out, rdMEM_t, stEXEC, wrGPR;
  wire [1:0] mp2_8b_1_p3_2;
  wire [3:0] rom_1_data_2;
  wire [5:0] kmadr_1_adr5__0, mp2_8b_1_p2, mp2_8b_1_p3, reg6_inc_ld_1_a5__0;
  wire [21:17] rom_1_data;

  not not_1 (not_1_out, in_1);
  KMADR kmadr_1 (
    .immed(ADDRBUS[0]), .memdir(ADDRBUS[1]), .regdir(ADDRBUS[2]), .memind(ADDRBUS[3]),
    .Adr5__0(kmadr_1_adr5__0), .preincr(ADDRBUS[4]), .postdec(ADDRBUS[5]), .regindpom(ADDRBUS[6]));
  // MP2_8b mp2_8b_1: pin names not known; wires that end beside it: bradr, {2'b00, mp2_8b_1_p2}, {mp2_8b_1_p3_2, mp2_8b_1_p3}, {2'b00, kmadr_1_adr5__0}, 1'b1
  REG6_INC_LD reg6_inc_ld_1 (
    .I5__0(mp2_8b_1_p3), .LD(or_1_out), .INC(not_2_out), .mr(not_1_out), .CLK(in_2),
    .A5__0(reg6_inc_ld_1_a5__0));
  not not_2 (not_2_out, or_1_out);
  Decoder #(.select(4), .disabled(0)) decoder_1 (
    .out1(bruncnd), .out2(brnotADDR), .out3(brSTOREorJSRorSTRLEN), .out4(brnotFCBUS), .out5(bradr),
    .sel(rom_1_data_2), .en(1'b1));  // open: out0, out6, out7, out8, out9, out10, out11, out12, out13, out14, out15
  or or_1 (or_1_out, bruncnd, brcnd, bradr);
  ROM #(.addrWidth(6), .dataWidth(32)) rom_1 (
    .addr(reg6_inc_ld_1_a5__0),
    .data({mp2_8b_1_p2, rom_1_data_2, rom_1_data, stEXEC, clADDR, wrGPR, decB, incB, incMAR, ldDWH, ldDWL, ldMDR, rdMEM_t, ldMAR, mxMAR2, mxMAR1, mxMAR0, ldB, mxB1, mxB0}),
    .sel(1'b1));
  not not_3 (not_3_out, PHASEFFBUS[1]);
  or or_2 (or_2_out, INSTRUCBUS[16], INSTRUCBUS[17], INSTRUCBUS[20]);
  not not_4 (not_4_out, in_3);
  and and_1 (and_1_out, not_3_out, brnotADDR);
  and and_2 (and_2_out, or_2_out, brSTOREorJSRorSTRLEN);
  and and_3 (and_3_out, brnotFCBUS, not_4_out);
  or or_3 (brcnd, and_1_out, and_2_out, and_3_out);
  assign CMEMBUS[0] = ldMAR ? 1'b1 : 1'bz;  // Controlled_Buffer controlled_buffer_1
  assign CMEMBUS[1] = incMAR ? 1'b1 : 1'bz;  // Controlled_Buffer controlled_buffer_2
  assign CMEMBUS[2] = ldMDR ? 1'b1 : 1'bz;  // Controlled_Buffer controlled_buffer_3
  assign CMEMBUS[5] = mxMAR0 ? 1'b1 : 1'bz;  // Controlled_Buffer controlled_buffer_4
  assign CMEMBUS[6] = mxMAR1 ? 1'b1 : 1'bz;  // Controlled_Buffer controlled_buffer_5
  assign CMEMBUS[7] = mxMAR2 ? 1'b1 : 1'bz;  // Controlled_Buffer controlled_buffer_6
  assign CFFBUS[3] = clADDR ? 1'b1 : 1'bz;  // Controlled_Buffer controlled_buffer_7
  assign CFFBUS[4] = stEXEC ? 1'b1 : 1'bz;  // Controlled_Buffer controlled_buffer_8
  assign CREGBUS[4] = ldB ? 1'b1 : 1'bz;  // Controlled_Buffer controlled_buffer_9
  assign CREGBUS[5] = mxB0 ? 1'b1 : 1'bz;  // Controlled_Buffer controlled_buffer_10
  assign CREGBUS[6] = mxB1 ? 1'b1 : 1'bz;  // Controlled_Buffer controlled_buffer_11
  assign CREGBUS[7] = incB ? 1'b1 : 1'bz;  // Controlled_Buffer controlled_buffer_12
  assign CREGBUS[8] = decB ? 1'b1 : 1'bz;  // Controlled_Buffer controlled_buffer_13
  assign CREGBUS[9] = wrGPR ? 1'b1 : 1'bz;  // Controlled_Buffer controlled_buffer_14
  assign CREGBUS[10] = ldDWL ? 1'b1 : 1'bz;  // Controlled_Buffer controlled_buffer_15
  assign CREGBUS[11] = ldDWH ? 1'b1 : 1'bz;  // Controlled_Buffer controlled_buffer_16
  assign rdMEM = rdMEM_t ? 1'b1 : 1'bz;  // Controlled_Buffer controlled_buffer_17

  // Other names for the same wires on the sheet: immed = ADDRBUS[0]; memdir = ADDRBUS[1]; regdir = ADDRBUS[2];
  //   memind = ADDRBUS[3]; preincr = ADDRBUS[4]; postdec = ADDRBUS[5]; regindpom = ADDRBUS[6]; CLK = in_2;
  //   FCBUS = in_3; HALT = INSTRUCBUS[0]; RTS = INSTRUCBUS[1]; RTI = INSTRUCBUS[2]; PUSHPSW = INSTRUCBUS[3];
  //   POPPSW = INSTRUCBUS[4]; PUSH = INSTRUCBUS[5]; POP = INSTRUCBUS[6]; INTE = INSTRUCBUS[7]; INTD = INSTRUCBUS[8];
  //   BOVF = INSTRUCBUS[9]; BNEQ = INSTRUCBUS[10]; BLEQU = INSTRUCBUS[11]; JLSS = INSTRUCBUS[12];
  //   JLEQ = INSTRUCBUS[13]; JMP = INSTRUCBUS[14]; LD = INSTRUCBUS[15]; ST = INSTRUCBUS[16]; JSR = INSTRUCBUS[17];
  //   TST = INSTRUCBUS[18]; XOR = INSTRUCBUS[19]; STRLEN = INSTRUCBUS[20]; ADD = INSTRUCBUS[21];
  //   FETCH = PHASEFFBUS[0]; ADDR = PHASEFFBUS[1]; EXEC = PHASEFFBUS[2]; INTR = PHASEFFBUS[3]; rst = in_1

  // Notes on the sheet:
  //   Operaciona jedinica
  //   Upravljacka jedinica
  //   contents of rom_1 (hex, n*v repeats v):
  //   800000 1400000 68400005 50400048 68400006 48 19000180 a00 21000180 400 50400058 6 1000 1000 50404060
  //   6e 2000 2000 50404000 50 68c00000 55000180 a00 5d000180 400 4 418000
endmodule

module EXEC (
  input  in_1,
  input  in_2,
  input  in_3,
  input  [3:0] PHASEFFBUS,
  input  [23:0] INSTRUCBUS,
  input  [7:0] ADDRBUS,
  input  [15:0] PSW,
  input  [15:0] B,
  input  [15:0] DW,
  input  [7:0] MDR,
  output [15:0] A,
  output [15:0] ALU,
  output C16,
  output [23:0] CMEMBUS,
  output [7:0] CFFBUS,
  output [23:0] CREGBUS,
  output [9:0] CPSW,
  output rdMEM,
  output wrMEM
);

  wire add_t, \and , and_1_out, and_3_out, and_4_out, and_5_out, and_6_out, and_7_out, and_8_out, and_9_out,
       and_10_out, and_11_out, and_12_out, brcnd, brnotbrorjmp, brnotEXEC, brnotFCBUS, bropr, brorjmp,
       brregdir, bruncnd, brzero, clA, clEXEC, clPSWI, clPSWSTART, decSP, incA, incMAR, incSP, ldA, ldC,
       ldDWH, ldDWL, ldI, ldMAR, ldMDR, ldN, ldPC, ldSTART, ldV, ldZ, mp2_8b_1_p3, mp4_16b_1_p5, mxA0, mxA1,
       mxDW, mxGPR, mxMAR1, mxMAR2, mxMDR0, mxMDR1, mxMDR2, mxPC0, mxPC1, not_1_out, not_2_out, not_4_out,
       not_5_out, not_6_out, or_2_out, or_3_out, rdMEM_t, reg8_inc_ld_1_p5, reg8_inc_ld_1_p6, stINTR, stPSWI,
       wrGPR, wrMEM_t, xor_1_out, xor_t, zero;
  wire [7:0] kmopr_1_adr7__0, mp2_8b_1_p2, reg8_inc_ld_1_p4;
  wire [19:7] rom_1_data;

  not not_1 (not_1_out, in_1);
  // MP4_16b mp4_16b_1: pin names not known; wires that end beside it: mxA1, mxA0, B, DW, mp4_16b_1_p5, ALU, 1'b1
  // REG16 reg16_1: pin names not known; wires that end beside it: clA, in_2, not_1_out, mp4_16b_1_p5, A, ldA, incA
  not not_2 (not_2_out, in_1);
  KMOPR kmopr_1 (
    .HALT(INSTRUCBUS[0]), .RTS(INSTRUCBUS[1]), .RTI(INSTRUCBUS[2]), .PUSHPSW(INSTRUCBUS[3]),
    .POPPSW(INSTRUCBUS[4]), .PUSH(INSTRUCBUS[5]), .POP(INSTRUCBUS[6]), .INTE(INSTRUCBUS[7]),
    .INTD(INSTRUCBUS[8]), .BOVF(INSTRUCBUS[9]), .BNEQ(INSTRUCBUS[10]), .Adr7__0(kmopr_1_adr7__0),
    .BLEQU(INSTRUCBUS[11]), .JLSS(INSTRUCBUS[12]), .JLEQ(INSTRUCBUS[13]), .JMP(INSTRUCBUS[14]),
    .LD(INSTRUCBUS[15]), .ST(INSTRUCBUS[16]), .JSR(INSTRUCBUS[17]), .TST(INSTRUCBUS[18]),
    .XOR(INSTRUCBUS[19]), .STRLEN(INSTRUCBUS[20]), .ADD(INSTRUCBUS[21]));
  // MP2_8b mp2_8b_1: pin names not known; wires that end beside it: bropr, mp2_8b_1_p2, mp2_8b_1_p3, kmopr_1_adr7__0, 1'b1, INSTRUCBUS[20], INSTRUCBUS[21]
  // REG8_INC_LD reg8_inc_ld_1: pin names not known; wires that end beside it: in_2, not_2_out, mp2_8b_1_p3, reg8_inc_ld_1_p4, reg8_inc_ld_1_p5, reg8_inc_ld_1_p6
  not not_3 (reg8_inc_ld_1_p6, reg8_inc_ld_1_p5);
  ROM #(.dataWidth(28)) rom_1 (
    .addr(reg8_inc_ld_1_p4),
    .data({mp2_8b_1_p2, rom_1_data, stINTR, clEXEC, incA, clA, add_t, xor_t, \and }), .sel(1'b1));
  or or_1 (reg8_inc_ld_1_p5, bruncnd, brcnd, bropr);
  Decoder #(.select(4), .disabled(0)) decoder_1 (
    .out1(bruncnd), .out2(brnotEXEC), .out3(brnotbrorjmp), .out4(brregdir), .out5(brzero), .out6(brnotFCBUS),
    .out7(bropr), .sel(rom_1_data[19:16]), .en(1'b1));  // open: out0, out8, out9, out10, out11, out12, out13, out14, out15
  ALU16_ADD_SUB_NOT_AND_OR_XOR alu16_add_sub_not_and_or_xor_1 (
    .Cin(1'b0), .A(A), .B(B), .add(add_t), .sub(1'b0), .\not (1'b0), .\and (\and ), .\or (1'b0),
    .\xor (xor_t), .F(ALU), .Cout(C16));
  ROM #(.dataWidth(32)) rom_2 (
    .addr(reg8_inc_ld_1_p4),
    .data({mxDW, wrGPR, mxGPR, incMAR, clPSWI, stPSWI, wrMEM_t, mxMDR0, mxMDR1, mxMDR2, incSP, ldA, mxA0, mxA1, ldSTART, ldI, ldV, ldC, ldZ, ldN, ldPC, mxPC0, mxPC1, ldDWL, ldDWH, ldMDR, rdMEM_t, decSP, ldMAR, mxMAR1, mxMAR2, clPSWSTART}),
    .sel(1'b1));
  and and_1 (and_1_out, ~MDR[0], ~MDR[1], ~MDR[2], ~MDR[3], ~MDR[4], ~MDR[5], ~MDR[6], ~MDR[7]);  // AND_Gate
  and and_2 (zero, and_1_out, INSTRUCBUS[20]);
  or or_2 (or_2_out, PSW[4], PSW[1]);
  xor xor_1 (xor_1_out, PSW[2], PSW[3]);
  not not_4 (not_4_out, PHASEFFBUS[2]);
  not not_5 (not_5_out, brorjmp);
  not not_6 (not_6_out, in_3);
  or or_3 (or_3_out, xor_1_out, PSW[1]);
  and and_3 (and_3_out, not_4_out, brnotEXEC);
  and and_4 (and_4_out, not_5_out, brnotbrorjmp);
  and and_5 (and_5_out, ADDRBUS[2], brregdir);
  and and_6 (and_6_out, zero, brzero);
  and and_7 (and_7_out, not_6_out, brnotFCBUS);
  and and_8 (and_8_out, PSW[3], INSTRUCBUS[9]);
  and and_9 (and_9_out, ~PSW[1], INSTRUCBUS[10]);  // AND_Gate
  and and_10 (and_10_out, or_2_out, INSTRUCBUS[11]);
  and and_11 (and_11_out, xor_1_out, INSTRUCBUS[12]);
  and and_12 (and_12_out, or_3_out, INSTRUCBUS[13]);
  or or_4 (brcnd, and_3_out, and_4_out, and_5_out, and_6_out, and_7_out);
  or or_5 (brorjmp, and_8_out, and_9_out, and_10_out, and_11_out, and_12_out);
  assign CMEMBUS[0] = ldMAR ? 1'b1 : 1'bz;  // Controlled_Buffer controlled_buffer_1
  assign CMEMBUS[1] = incMAR ? 1'b1 : 1'bz;  // Controlled_Buffer controlled_buffer_2
  assign CMEMBUS[2] = ldMDR ? 1'b1 : 1'bz;  // Controlled_Buffer controlled_buffer_3
  assign CMEMBUS[3] = ldPC ? 1'b1 : 1'bz;  // Controlled_Buffer controlled_buffer_4
  assign CMEMBUS[6] = mxMAR1 ? 1'b1 : 1'bz;  // Controlled_Buffer controlled_buffer_5
  assign CMEMBUS[7] = mxMAR2 ? 1'b1 : 1'bz;  // Controlled_Buffer controlled_buffer_6
  assign CMEMBUS[8] = mxMDR0 ? 1'b1 : 1'bz;  // Controlled_Buffer controlled_buffer_7
  assign CMEMBUS[9] = mxMDR1 ? 1'b1 : 1'bz;  // Controlled_Buffer controlled_buffer_8
  assign CMEMBUS[10] = mxMDR2 ? 1'b1 : 1'bz;  // Controlled_Buffer controlled_buffer_9
  assign CMEMBUS[11] = mxPC0 ? 1'b1 : 1'bz;  // Controlled_Buffer controlled_buffer_10
  assign CMEMBUS[12] = mxPC1 ? 1'b1 : 1'bz;  // Controlled_Buffer controlled_buffer_11
  assign CMEMBUS[13] = incSP ? 1'b1 : 1'bz;  // Controlled_Buffer controlled_buffer_12
  assign CMEMBUS[14] = decSP ? 1'b1 : 1'bz;  // Controlled_Buffer controlled_buffer_13
  assign CFFBUS[5] = clEXEC ? 1'b1 : 1'bz;  // Controlled_Buffer controlled_buffer_14
  assign CFFBUS[6] = stINTR ? 1'b1 : 1'bz;  // Controlled_Buffer controlled_buffer_15
  assign CREGBUS[9] = wrGPR ? 1'b1 : 1'bz;  // Controlled_Buffer controlled_buffer_16
  assign CREGBUS[10] = ldDWL ? 1'b1 : 1'bz;  // Controlled_Buffer controlled_buffer_17
  assign CREGBUS[11] = ldDWH ? 1'b1 : 1'bz;  // Controlled_Buffer controlled_buffer_18
  assign CREGBUS[12] = mxGPR ? 1'b1 : 1'bz;  // Controlled_Buffer controlled_buffer_19
  assign CREGBUS[13] = mxDW ? 1'b1 : 1'bz;  // Controlled_Buffer controlled_buffer_20
  assign CPSW[0] = clPSWSTART ? 1'b1 : 1'bz;  // Controlled_Buffer controlled_buffer_21
  assign CPSW[1] = ldI ? 1'b1 : 1'bz;  // Controlled_Buffer controlled_buffer_22
  assign CPSW[2] = ldC ? 1'b1 : 1'bz;  // Controlled_Buffer controlled_buffer_23
  assign CPSW[3] = ldV ? 1'b1 : 1'bz;  // Controlled_Buffer controlled_buffer_24
  assign CPSW[4] = ldN ? 1'b1 : 1'bz;  // Controlled_Buffer controlled_buffer_25
  assign CPSW[5] = ldZ ? 1'b1 : 1'bz;  // Controlled_Buffer controlled_buffer_26
  assign CPSW[6] = ldSTART ? 1'b1 : 1'bz;  // Controlled_Buffer controlled_buffer_27
  assign CPSW[7] = stPSWI ? 1'b1 : 1'bz;  // Controlled_Buffer controlled_buffer_28
  assign CPSW[8] = clPSWI ? 1'b1 : 1'bz;  // Controlled_Buffer controlled_buffer_29
  assign rdMEM = rdMEM_t ? 1'b1 : 1'bz;  // Controlled_Buffer controlled_buffer_30
  assign wrMEM = wrMEM_t ? 1'b1 : 1'bz;  // Controlled_Buffer controlled_buffer_31

  // Other names for the same wires on the sheet: A15__0[15:0] = A; immed = ADDRBUS[0]; memdir = ADDRBUS[1];
  //   regdir = ADDRBUS[2]; memind = ADDRBUS[3]; preincr = ADDRBUS[4]; postdec = ADDRBUS[5]; regindpom = ADDRBUS[6];
  //   ALU15__0[15:0] = ALU; B15__0[15:0] = B; CLK = in_2; DW15__0[15:0] = DW; FCBUS = in_3; HALT = INSTRUCBUS[0];
  //   RTS = INSTRUCBUS[1]; RTI = INSTRUCBUS[2]; PUSHPSW = INSTRUCBUS[3]; POPPSW = INSTRUCBUS[4]; PUSH = INSTRUCBUS[5];
  //   POP = INSTRUCBUS[6]; INTE = INSTRUCBUS[7]; INTD = INSTRUCBUS[8]; BOVF = INSTRUCBUS[9]; BNEQ = INSTRUCBUS[10];
  //   BLEQU = INSTRUCBUS[11]; JLSS = INSTRUCBUS[12]; JLEQ = INSTRUCBUS[13]; JMP = INSTRUCBUS[14]; LD = INSTRUCBUS[15];
  //   ST = INSTRUCBUS[16]; JSR = INSTRUCBUS[17]; TST = INSTRUCBUS[18]; XOR = INSTRUCBUS[19]; STRLEN = INSTRUCBUS[20];
  //   ADD = INSTRUCBUS[21]; MDR7__0[7:0] = MDR; FETCH = PHASEFFBUS[0]; ADDR = PHASEFFBUS[1]; EXEC = PHASEFFBUS[2];
  //   INTR = PHASEFFBUS[3]; PSWSTART = PSW[0]; PSWZ = PSW[1]; PSWN = PSW[2]; PSWV = PSW[3]; PSWC = PSW[4];
  //   PSWI = PSW[15]; rst = in_1

  // Notes on the sheet:
  //   Operaciona jedinica
  //   Upravljacka jedinica
  //   Akumulator
  //   contents of rom_1 (hex, n*v repeats v):
  //   20000 70000 5d10000 0 460000 0 0 760000 0 5d10000 0 b60000 0 0 e60000 0 0 0 1260000 0 0 1560000 0 0
  //   0 1960000 0 0 1c60000 0 5d10000 0 0 2160000 0 0 2460000 5d10000 0 2760000 0 0 2a60000 0 5d10000 0 0
  //   2f60000 0 0 3260000 5d10000 0 3560000 0 0 3860000 0 0 5d10000 5d10000 5d10000 5d30000 5d10000
  //   5d30000 5d10000 0 5d10000 4a40000 0 4660000 0 4860000 5d10000 5d10000 0 0 0 4e60000 0 0 5160000
  //   5d10000 5d10001 2 5d10000 8 5760000 5d50000 10 5710000 4 0 10060
  //   ALU
  //   contents of rom_2 (hex, n*v repeats v):
  //   0 0 1 1e 60 80 1e 60 100 a00 1e 60 80 1e 60 100 3f000 1e 60 80 1e 60 100 180000 1e 60 80 1e 60 100
  //   a00 200000 c0004e 2000000 200000 140004e 2000000 0 1e 60 80 1e 60 100 3f000 200000 100004e 2000000
  //   200000 80004e 2000000 0 1e 60 80 1e 60 100 180000 3000 4000000 8000000 0 c00 0 e00 100000 3000 0
  //   1000040 2000000 10800040 2000000 0 60000000 80000180 200000 40004e 2000000 200000 180004e 2000000
  //   a00 3000 140000 3000 0 60 0 10000000 3000 14c000 3000
  //   Signal zero
  //   Uslov za skok
endmodule

module INTR (
  input  in_1,
  input  in_2,
  input  in_3,
  input  [3:0] PHASEFFBUS,
  input  [23:0] INSTRUCBUS,
  input  [15:0] PSW,
  input  [7:0] intr,
  output [15:0] ADDIVTP,
  output [2:0] UEXT2__0,
  output inta,
  output [23:0] CMEMBUS,
  output [7:0] CFFBUS,
  output [23:0] CREGBUS,
  output rdMEM,
  output wrMEM
);

  wire and_2_out, and_3_out, and_4_out, brcnd, brnotFCBUS, brnotINTR, brnotprekid, bruncnd, clINTR, incMAR,
       incSP, ldDWH, ldDWL, ldMAR, ldMDR, ldPC, mxMAR0, mxMAR1, mxMAR2, mxMDR0, mxMDR1, mxMDR2, mxPC1,
       not_1_out, not_2_out, not_3_out, not_4_out, not_5_out, not_6_out, not_7_out, or_2_out, prekid, prper,
       rdMEM_t, stFETCH, wrMEM_t;
  wire [2:0] rom_1_data_2;
  wire [3:1] IVTDSP15__0;
  wire [5:0] reg6_inc_ld_1_a5__0, rom_1_data;
  wire [15:0] IVTP15__0;
  wire [22:19] rom_1_data_3;

  and and_1 (prekid, prper, PSW[15], not_3_out);
  not not_1 (not_1_out, in_1);
  not not_2 (not_2_out, in_1);
  REG6_INC_LD reg6_inc_ld_1 (
    .I5__0(rom_1_data), .LD(or_2_out), .INC(not_4_out), .mr(not_2_out), .CLK(in_2),
    .A5__0(reg6_inc_ld_1_a5__0));
  or or_1 (prper, intr[7], intr[6], intr[5], intr[4], intr[3], intr[2], intr[1], intr[0]);
  not not_3 (not_3_out, INSTRUCBUS[0]);
  // REG16_LD reg16_ld_1: pin names not known; wires that end beside it: in_2, not_1_out, IVTP15__0
  not not_4 (not_4_out, or_2_out);
  Decoder #(.select(3), .disabled(0)) decoder_1 (
    .out1(bruncnd), .out2(brnotINTR), .out3(brnotprekid), .out4(brnotFCBUS), .sel(rom_1_data_2), .en(1'b1));  // open: out0, out5, out6, out7
  or or_2 (or_2_out, bruncnd, brcnd);
  ROM #(.addrWidth(6), .dataWidth(32)) rom_1 (
    .addr(reg6_inc_ld_1_a5__0),
    .data({rom_1_data, rom_1_data_2, rom_1_data_3, stFETCH, clINTR, ldPC, mxPC1, ldDWH, ldDWL, incMAR, inta, rdMEM_t, wrMEM_t, ldMDR, mxMDR0, mxMDR1, mxMDR2, ldMAR, mxMAR0, mxMAR1, mxMAR2, incSP}),
    .sel(1'b1));
  PCD8 pcd8_1 (
    .En(1'b1), .C7(intr[7]), .C6(intr[6]), .C5(intr[5]), .C4(intr[4]), .C3(intr[3]), .C2(intr[2]),
    .C1(intr[1]), .C0(intr[0]), .Z2(UEXT2__0[2]), .Z1(UEXT2__0[1]), .Z0(UEXT2__0[0]));  // open: W
  // REG3_LD reg3_ld_1: pin names not known; wires that end beside it: in_2, UEXT2__0, IVTDSP15__0, inta
  not not_5 (not_5_out, PHASEFFBUS[3]);
  not not_6 (not_6_out, prekid);
  not not_7 (not_7_out, in_3);
  // ADD16 add16_1: pin names not known; wires that end beside it: IVTP15__0, ADDIVTP, {{12{1'b0}}, IVTDSP15__0, 1'b0}, 1'b0
  and and_2 (and_2_out, not_5_out, brnotINTR);
  and and_3 (and_3_out, not_6_out, brnotprekid);
  and and_4 (and_4_out, not_7_out, brnotFCBUS);
  or or_3 (brcnd, and_2_out, and_3_out, and_4_out);
  assign CMEMBUS[0] = ldMAR ? 1'b1 : 1'bz;  // Controlled_Buffer controlled_buffer_1
  assign CMEMBUS[1] = incMAR ? 1'b1 : 1'bz;  // Controlled_Buffer controlled_buffer_2
  assign CMEMBUS[2] = ldMDR ? 1'b1 : 1'bz;  // Controlled_Buffer controlled_buffer_3
  assign CMEMBUS[3] = ldPC ? 1'b1 : 1'bz;  // Controlled_Buffer controlled_buffer_4
  assign CMEMBUS[5] = mxMAR0 ? 1'b1 : 1'bz;  // Controlled_Buffer controlled_buffer_5
  assign CMEMBUS[6] = mxMAR1 ? 1'b1 : 1'bz;  // Controlled_Buffer controlled_buffer_6
  assign CMEMBUS[7] = mxMAR2 ? 1'b1 : 1'bz;  // Controlled_Buffer controlled_buffer_7
  assign CMEMBUS[8] = mxMDR0 ? 1'b1 : 1'bz;  // Controlled_Buffer controlled_buffer_8
  assign CMEMBUS[9] = mxMDR1 ? 1'b1 : 1'bz;  // Controlled_Buffer controlled_buffer_9
  assign CMEMBUS[10] = mxMDR2 ? 1'b1 : 1'bz;  // Controlled_Buffer controlled_buffer_10
  assign CMEMBUS[12] = mxPC1 ? 1'b1 : 1'bz;  // Controlled_Buffer controlled_buffer_11
  assign CMEMBUS[13] = incSP ? 1'b1 : 1'bz;  // Controlled_Buffer controlled_buffer_12
  assign CFFBUS[0] = stFETCH ? 1'b1 : 1'bz;  // Controlled_Buffer controlled_buffer_13
  assign CFFBUS[7] = clINTR ? 1'b1 : 1'bz;  // Controlled_Buffer controlled_buffer_14
  assign CREGBUS[10] = ldDWL ? 1'b1 : 1'bz;  // Controlled_Buffer controlled_buffer_15
  assign CREGBUS[11] = ldDWH ? 1'b1 : 1'bz;  // Controlled_Buffer controlled_buffer_16
  assign rdMEM = rdMEM_t ? 1'b1 : 1'bz;  // Controlled_Buffer controlled_buffer_17
  assign wrMEM = wrMEM_t ? 1'b1 : 1'bz;  // Controlled_Buffer controlled_buffer_18

  // Other names for the same wires on the sheet: ldBR = inta; ADDIVTP15__0[15:0] = ADDIVTP; CLK = in_2; FCBUS = in_3;
  //   HALT = INSTRUCBUS[0]; RTS = INSTRUCBUS[1]; RTI = INSTRUCBUS[2]; PUSHPSW = INSTRUCBUS[3]; POPPSW = INSTRUCBUS[4];
  //   PUSH = INSTRUCBUS[5]; POP = INSTRUCBUS[6]; INTE = INSTRUCBUS[7]; INTD = INSTRUCBUS[8]; BOVF = INSTRUCBUS[9];
  //   BNEQ = INSTRUCBUS[10]; BLEQU = INSTRUCBUS[11]; JLSS = INSTRUCBUS[12]; JLEQ = INSTRUCBUS[13];
  //   JMP = INSTRUCBUS[14]; LD = INSTRUCBUS[15]; ST = INSTRUCBUS[16]; JSR = INSTRUCBUS[17]; TST = INSTRUCBUS[18];
  //   XOR = INSTRUCBUS[19]; STRLEN = INSTRUCBUS[20]; ADD = INSTRUCBUS[21]; intr7__0[7:0] = intr;
  //   FETCH = PHASEFFBUS[0]; ADDR = PHASEFFBUS[1]; EXEC = PHASEFFBUS[2]; INTR_t = PHASEFFBUS[3]; PSWSTART = PSW[0];
  //   PSWZ = PSW[1]; PSWN = PSW[2]; PSWV = PSW[3]; PSWC = PSW[4]; PSWI = PSW[15]; rst = in_1

  // Notes on the sheet:
  //   Operaciona jedinica
  //   Upravljacka jedinica
  //   contents of rom_1 (hex, n*v repeats v):
  //   1000000 6d800000 1 136 12000200 1 1d6 1e000200 1 196 2a000200 1 156 36000200 1 176 42000200 1 1b6
  //   4e000200 800 1e 5a000500 3000 62000500 4000 18000 860000
endmodule

module RAM (
  input  [15:0] in_1,
  input  in_2,
  input  [7:0] in_3,
  input  in_4,
  input  in_5,
  input  in_6,
  output [7:0] out_7,
  output out_8
);

  wire and_1_out, and_2_out, CNT0, LDCNT, not_1_out, notCNT0, or_1_out, reg4_ld_sl_sr_1_p6, rsff_2_p4,
       rsff_2_p5, rsff_3_p4, sl;
  wire [3:0] CNT, LFSR;

  // RSFF rsff_1: pin names not known; wires that end beside it: 1'b0, in_2, in_6, sl
  or or_1 (or_1_out, in_4, in_5);
  // REG4_LD_SL_SR reg4_ld_sl_sr_1: pin names not known; wires that end beside it: 1'b0, 1'b0, in_2, 4'b1111, LFSR, reg4_ld_sl_sr_1_p6, sl, in_6
  // RisingEdge risingedge_1: pin names not known; wires that end beside it: or_1_out, in_2, LDCNT
  // MEM64Kx8 mem64kx8_1: pin names not known; wires that end beside it: in_1, 1'b1, in_2, in_3, out_7, in_4
  xor xor_1 (reg4_ld_sl_sr_1_p6, LFSR[2], LFSR[3]);
  and and_1 (and_1_out, CNT0, not_1_out);
  not not_1 (not_1_out, LDCNT);
  // RSFF rsff_2: pin names not known; wires that end beside it: and_1_out, in_2, LDCNT, rsff_2_p4, rsff_2_p5
  not not_2 (rsff_2_p4, in_6);
  and and_2 (and_2_out, rsff_2_p5, CNT0);
  // REG4m_DEC_LD reg4m_dec_ld_1: pin names not known; wires that end beside it: in_2, LFSR, CNT, LDCNT, notCNT0, notCNT0
  or or_2 (notCNT0, CNT[0], CNT[1], CNT[2], CNT[3]);
  // RSFF rsff_3: pin names not known; wires that end beside it: out_8, in_2, and_2_out, rsff_3_p4, out_8
  not not_3 (rsff_3_p4, in_6);
  not not_4 (CNT0, notCNT0);

  // Other names for the same wires on the sheet: ADR[15:0] = in_1; CLK = in_2; DIN[7:0] = in_3; DOUT[7:0] = out_7;
  //   fc = out_8; RDMEM = in_5; rst = in_6; WRMEM = in_4

  // Notes on the sheet:
  //   Random broj predstavlja vreme pristupa memoriji
  //   Brojac za generisanje random broja 
  //   Jedinica za generisanje function complete (fc) signala
  //   Brojac za dekrementiranje random broja
endmodule
